// Logisim project Question 3.24 Logic.circ as structural Verilog: 1 circuit, main circuit main
module main (
  input  T_A,
  input  T_B,
  output LA1,
  output LA0,
  output C,
  output LB1,
  output LB0
);

  wire and_1_out, and_2_out, and_3_out, and_4_out, and_5_out, and_6_out, and_7_out, and_8_out, and_9_out,
       and_10_out, and_11_out, and_12_out, and_14_out, and_15_out, and_16_out, and_18_out, and_19_out,
       and_20_out, and_21_out, and_22_out, and_23_out, clock_1_out, d_ff_1_q, d_ff_2_q, d_ff_3_q, d_ff_4_q,
       nor_1_out, not_1_out, not_2_out, not_3_out, not_4_out, not_5_out, not_6_out, not_7_out, not_8_out,
       not_9_out, not_10_out, not_11_out, not_12_out, not_13_out, not_14_out, not_15_out, not_16_out,
       not_17_out, not_18_out, not_19_out, not_20_out, or_1_out, or_2_out, or_3_out, S0_q, S1_q, S2_q;

  nor nor_1 (nor_1_out, C, d_ff_4_q, d_ff_3_q, d_ff_2_q, d_ff_1_q);
  and and_1 (and_1_out, and_20_out, and_19_out, nor_1_out);
  D_Flip_Flop d_ff_1 (.clk(clock_1_out), .D(and_1_out), .Q(d_ff_1_q));  // open: Qn, preset, en, reset
  D_Flip_Flop d_ff_2 (.clk(clock_1_out), .D(d_ff_1_q), .Q(d_ff_2_q));  // open: Qn, preset, en, reset
  D_Flip_Flop d_ff_3 (.clk(clock_1_out), .D(d_ff_2_q), .Q(d_ff_3_q));  // open: Qn, preset, en, reset
  D_Flip_Flop d_ff_4 (.clk(clock_1_out), .D(d_ff_3_q), .Q(d_ff_4_q));  // open: Qn, preset, en, reset
  D_Flip_Flop d_ff_5 (.clk(clock_1_out), .D(d_ff_4_q), .Q(C));  // open: Qn, preset, en, reset
  not not_1 (not_1_out, T_B);
  not not_2 (not_2_out, S0_q);
  not not_3 (not_3_out, C);
  not not_4 (not_4_out, S2_q);
  not not_5 (not_5_out, S1_q);
  not not_6 (not_6_out, S0_q);
  not not_7 (not_7_out, S1_q);
  not not_8 (not_8_out, S0_q);
  not not_9 (not_9_out, T_A);
  not not_10 (not_10_out, S0_q);
  not not_11 (not_11_out, S0_q);
  not not_12 (not_12_out, C);
  and and_2 (and_2_out, S1_q, S0_q, not_1_out);
  and and_3 (and_3_out, S2_q, not_2_out);
  and and_4 (and_4_out, S2_q, not_3_out);
  and and_5 (and_5_out, not_4_out, not_5_out, S0_q);
  and and_6 (and_6_out, S1_q, not_6_out);
  and and_7 (and_7_out, S1_q, T_B);
  and and_8 (and_8_out, not_7_out, not_8_out, not_9_out);
  and and_9 (and_9_out, S1_q, not_10_out, C);
  and and_10 (and_10_out, S1_q, S0_q, T_B);
  and and_11 (and_11_out, S2_q, not_11_out);
  and and_12 (and_12_out, S2_q, not_12_out);
  or or_1 (or_1_out, and_2_out, and_3_out, and_4_out);
  or or_2 (or_2_out, and_5_out, and_6_out, and_7_out);
  or or_3 (or_3_out, and_8_out, and_9_out, and_10_out, and_11_out, and_12_out);
  Clock clock_1 (.out(clock_1_out));
  D_Flip_Flop S2 (.clk(clock_1_out), .D(or_1_out), .Q(S2_q));  // open: Qn, preset, en, reset
  D_Flip_Flop S1 (.clk(clock_1_out), .D(or_2_out), .Q(S1_q));  // open: Qn, preset, en, reset
  D_Flip_Flop S0 (.clk(clock_1_out), .D(or_3_out), .Q(S0_q));  // open: Qn, preset, en, reset
  or or_4 (LA1, S1_q, S2_q);
  not not_13 (not_13_out, S2_q);
  not not_14 (not_14_out, S1_q);
  not not_15 (not_15_out, S2_q);
  not not_16 (not_16_out, S1_q);
  not not_17 (not_17_out, S2_q);
  not not_18 (not_18_out, S0_q);
  not not_19 (not_19_out, S1_q);
  not not_20 (not_20_out, S0_q);
  and and_13 (LA0, not_13_out, not_14_out, S0_q);
  and and_14 (and_14_out, not_15_out, not_16_out);
  and and_15 (and_15_out, not_17_out, not_18_out);
  and and_16 (and_16_out, not_19_out, S0_q);
  and and_17 (LB0, S2_q, not_20_out);
  LED LA (.in(and_18_out));
  LED LA_2 (.in(and_19_out));
  and and_18 (and_18_out, LA0, ~LA1);  // AND_Gate
  and and_19 (and_19_out, LA1, ~LA0);  // AND_Gate
  or or_5 (LB1, and_14_out, and_15_out, and_16_out);
  and and_20 (and_20_out, LB1, ~LB0);  // AND_Gate
  LED LB (.in(and_20_out));
  LED LA_3 (.in(and_21_out));
  and and_21 (and_21_out, ~LA1, ~LA0);  // AND_Gate
  and and_22 (and_22_out, LB0, ~LB1);  // AND_Gate
  and and_23 (and_23_out, ~LB0, ~LB1);  // AND_Gate
  LED LB_2 (.in(and_23_out));
  LED LB_3 (.in(and_22_out));
endmodule
