// Logisim project Question 3.26 Logic.circ as structural Verilog: 1 circuit, main circuit main
module main (
  input  Quarter,
  input  Dime,
  input  Nickel,
  output Return_Two_Dimes,
  output Return_Dime,
  output Return_Nickel,
  output Dispense
);

  wire and_1_out, and_2_out, and_3_out, and_4_out, and_5_out, and_6_out, and_7_out, and_8_out, and_9_out,
       and_10_out, and_11_out, and_12_out, and_13_out, and_14_out, and_15_out, clock_1_out, or_1_out,
       or_2_out, or_3_out, or_4_out, or_5_out, or_6_out, s0_q, s1_q, s2_q, s3_q, s4_q, s5_q, s6_q, s7_q, s8_q;

  and and_1 (and_1_out, Quarter, s0_q);
  or or_1 (or_1_out, Return_Two_Dimes, s8_q, s7_q, s6_q, s5_q);
  and and_2 (and_2_out, Dime, s0_q);
  and and_3 (and_3_out, Nickel, s0_q);
  D_Flip_Flop s0 (.clk(clock_1_out), .D(or_1_out), .Q(s0_q));  // open: Qn, preset, en, reset
  D_Flip_Flop s1 (.clk(clock_1_out), .D(and_3_out), .Q(s1_q));  // open: Qn, preset, en, reset
  Clock clock_1 (.out(clock_1_out));
  and and_4 (and_4_out, Quarter, s1_q);
  and and_5 (and_5_out, Nickel, s1_q);
  or or_2 (or_2_out, and_2_out, and_5_out);
  and and_6 (and_6_out, Quarter, s2_q);
  and and_7 (and_7_out, Nickel, s2_q);
  and and_8 (and_8_out, Dime, s1_q);
  D_Flip_Flop s2 (.clk(clock_1_out), .D(or_2_out), .Q(s2_q));  // open: Qn, preset, en, reset
  and and_9 (and_9_out, Dime, s2_q);
  D_Flip_Flop s3 (.clk(clock_1_out), .D(or_3_out), .Q(s3_q));  // open: Qn, preset, en, reset
  or or_3 (or_3_out, and_7_out, and_8_out);
  and and_10 (and_10_out, Quarter, s3_q);
  and and_11 (and_11_out, Dime, s3_q);
  and and_12 (and_12_out, Nickel, s3_q);
  or or_4 (or_4_out, and_12_out, and_9_out);
  D_Flip_Flop s4 (.clk(clock_1_out), .D(or_4_out), .Q(s4_q));  // open: Qn, preset, en, reset
  and and_13 (and_13_out, Dime, s4_q);
  or or_5 (or_5_out, and_11_out, and_14_out, and_1_out);
  and and_14 (and_14_out, Nickel, s4_q);
  D_Flip_Flop s5 (.clk(clock_1_out), .D(or_5_out), .Q(s5_q));  // open: Qn, preset, en, reset
  D_Flip_Flop s6 (.clk(clock_1_out), .D(or_6_out), .Q(s6_q));  // open: Qn, preset, en, reset
  or or_6 (or_6_out, and_13_out, and_4_out);
  and and_15 (and_15_out, Quarter, s4_q);
  D_Flip_Flop s9 (.clk(clock_1_out), .D(and_15_out), .Q(Return_Two_Dimes));  // open: Qn, preset, en, reset
  D_Flip_Flop s8 (.clk(clock_1_out), .D(and_10_out), .Q(s8_q));  // open: Qn, preset, en, reset
  D_Flip_Flop s7 (.clk(clock_1_out), .D(and_6_out), .Q(s7_q));  // open: Qn, preset, en, reset
  or or_7 (Return_Dime, s8_q, s7_q);
  or or_8 (Return_Nickel, s8_q, s6_q);
  or or_9 (Dispense, Return_Two_Dimes, s8_q, s7_q, s6_q, s5_q);
endmodule
